// Logisim project 1_yanip_sonen_led.circ as structural Verilog: 1 circuit, main circuit main
module main (
  output out_1
);

  wire clock_1_out, d_ff_1_q;

  Clock clock_1 (.out(clock_1_out));
  D_Flip_Flop d_ff_1 (.clk(clock_1_out), .D(out_1), .Q(d_ff_1_q));  // open: Qn, preset, en, reset
  not not_1 (out_1, d_ff_1_q);
endmodule
