// Logisim project 2_iki_ledi_yakip_sondurme.circ as structural Verilog: 1 circuit, main circuit main
module main (
  output Y,
  output Z
);

  wire clock_1_out, S0_q, S0_qn, S1_q, S1_qn, xor_1_out;

  Clock clock_1 (.out(clock_1_out));
  D_Flip_Flop S0 (.clk(clock_1_out), .D(S0_qn), .Q(S0_q), .Qn(S0_qn));  // open: preset, en, reset
  D_Flip_Flop S1 (.clk(clock_1_out), .D(xor_1_out), .Q(S1_q), .Qn(S1_qn));  // open: preset, en, reset
  xor xor_1 (xor_1_out, S0_q, S1_q);
  and and_1 (Y, S0_qn, S1_qn);
  and and_2 (Z, S0_qn, S1_q);
endmodule
