// Logisim project 3_trafik_isigi.circ as structural Verilog: 1 circuit, main circuit main
module main (
);

  wire and_1_out, clock_1_out, S0_q, S0_qn, S1_q, S1_qn, xnor_1_out, xor_1_out;

  Clock clock_1 (.out(clock_1_out));
  D_Flip_Flop S1 (.clk(clock_1_out), .D(xor_1_out), .Q(S1_q), .Qn(S1_qn));  // open: preset, en, reset
  D_Flip_Flop S0 (.clk(clock_1_out), .D(S0_qn), .Q(S0_q), .Qn(S0_qn));  // open: preset, en, reset
  xnor xnor_1 (xnor_1_out, S1_q, S0_q);
  and and_1 (and_1_out, S1_qn, S0_q);
  xor xor_1 (xor_1_out, S1_q, S0_q);
  LED K (.in(xnor_1_out));
  LED S (.in(S0_qn));
  LED Y (.in(and_1_out));
endmodule
