// Logisim project 4_asansor.circ as structural Verilog: 1 circuit, main circuit main
module main (
  input  a,
  input  b,
  output out_3
);

  wire and_1_out, and_2_out, and_3_out, clock_1_out, not_1_out, S_q;

  Clock clock_1 (.out(clock_1_out));
  D_Flip_Flop S (.clk(clock_1_out), .D(out_3), .Q(S_q));  // open: Qn, preset, en, reset
  not not_1 (not_1_out, a);
  and and_1 (and_1_out, S_q, b);
  or or_1 (out_3, and_1_out, and_2_out, and_3_out);
  and and_2 (and_2_out, not_1_out, b);
  and and_3 (and_3_out, S_q, not_1_out);

  // Notes on the sheet:
  //   0. kat
  //   1. kat
endmodule
