// Logisim project saat.circ as structural Verilog: 3 circuits, main circuit main
module main (
  output out_1,
  output out_2
);

  wire and_1_out, button_1_out, clock_1_out, n7_segment_display_driver_1_p6, n7_segment_display_driver_1_p7,
       n7_segment_display_driver_1_p8, n7_segment_display_driver_1_p9, n7_segment_display_driver_1_p14,
       n7_segment_display_driver_1_p15, n7_segment_display_driver_1_p16, n7_segment_display_driver_1_p17,
       n7_segment_display_driver_1_p18, n7_segment_display_driver_1_p19, n7_segment_display_driver_1_p20,
       n60_counter_1__2, n60_counter_1__4, n60_counter_1__8, n60_counter_1__16, n60_counter_1__32, not_1_out,
       not_2_out, not_3_out, not_4_out, not_5_out, not_6_out;

  Clock clock_1 (.out(clock_1_out));
  Button button_1 (.out(button_1_out));
  _60_counter u_60_counter_1 (
    .\input (1'b1), .Clock(clock_1_out), ._59(button_1_out), ._1(out_1), ._2(n60_counter_1__2),
    ._4(n60_counter_1__4), ._8(n60_counter_1__8), ._16(n60_counter_1__16), ._32(n60_counter_1__32));  // open: Reset
  not not_1 (not_1_out, out_1);
  not not_2 (not_2_out, n60_counter_1__2);
  not not_3 (not_3_out, n60_counter_1__4);
  not not_4 (not_4_out, n60_counter_1__8);
  not not_5 (not_5_out, n60_counter_1__16);
  not not_6 (not_6_out, n60_counter_1__32);
  // _7_segment_display_driver 7_segment_display_driver_1: pin names not known; wires that end beside it: n60_counter_1__2, n60_counter_1__4, n60_counter_1__8, n60_counter_1__16, n60_counter_1__32, n7_segment_display_driver_1_p6, n7_segment_display_driver_1_p7, n7_segment_display_driver_1_p8, n7_segment_display_driver_1_p9, n7_segment_display_driver_1_p6, n7_segment_display_driver_1_p7, n7_segment_display_driver_1_p8, n7_segment_display_driver_1_p9, n7_segment_display_driver_1_p14, n7_segment_display_driver_1_p15, n7_segment_display_driver_1_p16, n7_segment_display_driver_1_p17, n7_segment_display_driver_1_p18, n7_segment_display_driver_1_p19, n7_segment_display_driver_1_p20
  and and_1 (and_1_out, not_1_out, not_2_out, not_3_out, not_4_out, not_5_out, not_6_out);
  _60_counter u_60_counter_2 (
    .\input (and_1_out), .Clock(clock_1_out), ._59(button_1_out), ._1(out_2));  // open: Reset, _2, _4, _8, _16, _32
  _7_Segment_Display u_7_segment_display_1 (
    .g(n7_segment_display_driver_1_p20), .f(n7_segment_display_driver_1_p19),
    .a(n7_segment_display_driver_1_p14), .b(n7_segment_display_driver_1_p15),
    .e(n7_segment_display_driver_1_p18), .d(n7_segment_display_driver_1_p17),
    .c(n7_segment_display_driver_1_p16));  // open: dp
endmodule

module _60_counter (
  input  \input ,
  input  Clock,
  input  Reset,
  input  _59,
  output _1,
  output _2,
  output _4,
  output _8,
  output _16,
  output _32
);

  wire and_1_out, and_2_out, and_3_out, and_4_out, and_5_out, and_6_out, j_k_ff_1_qn, j_k_ff_2_qn, or_1_out,
       or_2_out;

  and and_1 (and_1_out, _32, _16, _8, _4, j_k_ff_2_qn, j_k_ff_1_qn);
  J_K_Flip_Flop j_k_ff_1 (
    .J(\input ), .clk(Clock), .K(\input ), .Q(_1), .Qn(j_k_ff_1_qn), .preset(_59), .reset(or_1_out));  // open: en
  or or_1 (or_1_out, and_1_out, Reset);
  and and_2 (and_2_out, \input , _1);
  J_K_Flip_Flop j_k_ff_2 (
    .J(and_2_out), .clk(Clock), .K(and_2_out), .Q(_2), .Qn(j_k_ff_2_qn), .preset(_59), .reset(or_1_out));  // open: en
  and and_3 (and_3_out, and_2_out, _2);
  and and_4 (and_4_out, and_3_out, _4);
  J_K_Flip_Flop j_k_ff_3 (.J(and_3_out), .clk(Clock), .K(and_3_out), .Q(_4), .reset(or_2_out));  // open: Qn, preset, en
  or or_2 (or_2_out, _59, or_1_out);
  J_K_Flip_Flop j_k_ff_4 (
    .J(and_4_out), .clk(Clock), .K(and_4_out), .Q(_8), .preset(_59), .reset(or_1_out));  // open: Qn, en
  and and_5 (and_5_out, and_4_out, _8);
  and and_6 (and_6_out, and_5_out, _16);
  J_K_Flip_Flop j_k_ff_5 (
    .J(and_5_out), .clk(Clock), .K(and_5_out), .Q(_16), .preset(_59), .reset(or_1_out));  // open: Qn, en
  J_K_Flip_Flop j_k_ff_6 (
    .J(and_6_out), .clk(Clock), .K(and_6_out), .Q(_32), .preset(_59), .reset(or_1_out));  // open: Qn, en
endmodule

module _24_counter (
  input  \input ,
  input  Clock,
  input  Reset,
  input  in_4,
  output _1,
  output _2,
  output _4,
  output _8,
  output _16
);

  wire and_1_out, and_2_out, and_3_out, and_4_out, and_5_out, j_k_ff_1_qn, j_k_ff_2_qn, j_k_ff_3_qn, or_1_out;

  and and_1 (and_1_out, _16, _8, j_k_ff_3_qn, j_k_ff_2_qn, j_k_ff_1_qn);
  J_K_Flip_Flop j_k_ff_1 (
    .J(\input ), .clk(Clock), .K(\input ), .Q(_1), .Qn(j_k_ff_1_qn), .reset(or_1_out));  // open: preset, en
  or or_1 (or_1_out, and_1_out, Reset);
  J_K_Flip_Flop j_k_ff_2 (
    .J(and_2_out), .clk(Clock), .K(and_2_out), .Q(_2), .Qn(j_k_ff_2_qn), .preset(in_4), .reset(or_1_out));  // open: en
  and and_2 (and_2_out, \input , _1);
  // OR_Gate or_2 is placed but not wired
  and and_3 (and_3_out, and_2_out, _2);
  and and_4 (and_4_out, and_3_out, _4);
  J_K_Flip_Flop j_k_ff_3 (
    .J(and_3_out), .clk(Clock), .K(and_3_out), .Q(_4), .Qn(j_k_ff_3_qn), .reset(or_1_out));  // open: preset, en
  J_K_Flip_Flop j_k_ff_4 (
    .J(and_4_out), .clk(Clock), .K(and_4_out), .Q(_8), .preset(in_4), .reset(or_1_out));  // open: Qn, en
  and and_5 (and_5_out, and_4_out, _8);
  J_K_Flip_Flop j_k_ff_5 (
    .J(and_5_out), .clk(Clock), .K(and_5_out), .Q(_16), .preset(in_4), .reset(or_1_out));  // open: Qn, en
endmodule
